// Logisim project Hardware.circ as structural Verilog: 1 circuit, main circuit main
module main (
  input  Letter,
  input  in_2,
  input  Enable_Decrypt,
  input  E_1,
  input  in_5,
  input  N,
  input  in_7,
  input  in_8,
  input  in_9,
  output Output,
  output out_11,
  output out_12,
  output out_13
);

  wire clock_1_out, Load_out, multiplexer_7_out, multiplexer_8_out, not_1_out, not_2_out, or_1_out, Reset_out;
  wire [1:0] counter_1_q, multiplexer_1_out;
  wire [3:0] multiplexer_3_out, multiplier_1_out, register_1_q;

  Button Load (.out(Load_out));
  Multiplexer #(.enable("false")) multiplexer_1 (
    .in0(in_2), .in1(out_13), .out(multiplexer_1_out[0]), .sel(Enable_Decrypt));
  Multiplexer #(.enable("false")) multiplexer_2 (
    .in0(Letter), .in1(Output), .out(multiplexer_1_out[1]), .sel(Enable_Decrypt));
  Multiplier #(.width(4)) multiplier_1 (
    .a({2'b00, multiplexer_1_out}), .b(register_1_q), .out(multiplier_1_out));  // open: cin, cout
  Multiplexer #(.enable("false")) multiplexer_3 (
    .in0(multiplexer_1_out[0]), .in1(multiplier_1_out[0]), .out(multiplexer_3_out[0]), .sel(not_1_out));
  Multiplexer #(.enable("false")) multiplexer_4 (
    .in0(multiplexer_1_out[1]), .in1(multiplier_1_out[1]), .out(multiplexer_3_out[1]), .sel(not_1_out));
  Multiplexer #(.enable("false")) multiplexer_5 (
    .in0(1'b0), .in1(multiplier_1_out[2]), .out(multiplexer_3_out[2]), .sel(not_1_out));
  Multiplexer #(.enable("false")) multiplexer_6 (
    .in0(1'b0), .in1(multiplier_1_out[3]), .out(multiplexer_3_out[3]), .sel(not_1_out));
  not not_1 (not_1_out, Load_out);
  not not_2 (not_2_out, multiplexer_7_out);
  Register #(.width(4), .trigger("falling")) register_1 (
    .D(multiplexer_3_out), .Q(register_1_q), .clk(not_2_out), .clr(Reset_out));  // open: en
  Counter #(.width(2), .max('h3)) counter_1 (
    .load(1'b1), .D({E_1, in_5}), .count(not_1_out), .Q(counter_1_q), .clk(multiplexer_7_out), .clr(Reset_out));  // open: carry
  Button Reset (.out(Reset_out));
  Multiplexer #(.enable("false")) multiplexer_7 (
    .in0(multiplexer_8_out), .in1(Load_out), .out(multiplexer_7_out), .sel(Load_out));
  or or_1 (or_1_out, counter_1_q[0], counter_1_q[1]);
  Divider #(.width(4)) divider_1 (
    .a(register_1_q), .b({N, in_7, in_8, in_9}), .rem({Output, out_11, out_12, out_13}));  // open: out, upper
  Clock clock_1 (.out(clock_1_out));
  Multiplexer #(.enable("false")) multiplexer_8 (
    .in0(1'b0), .in1(clock_1_out), .out(multiplexer_8_out), .sel(or_1_out));
endmodule
