// Logisim project RSA.circ as structural Verilog: 4 circuits, main circuit main
module main (
  input  Load,
  input  [3:0] Prime1,
  input  [3:0] Prime2,
  input  Reset_E,
  input  Reset_D,
  input  Reset,
  input  Load_2,
  input  Clear,
  input  Reset_2,
  output [7:0] Encrypted_Data,
  output [7:0] N,
  output [7:0] E,
  output [7:0] Count,
  output [7:0] D,
  output [7:0] Rem1,
  output [7:0] Rem2,
  output [15:0] K,
  output [7:0] Phi,
  output [7:0] Count_2
);

  wire button_1_out, Button_2_out, Button_3_out, E_button_out, K_button_out, not_1_out, Write_out;
  wire [6:0] decrypter_1_letter, keyboard_1_data;

  KeyGenerator keygenerator_1 (
    .P(Prime1), .Q(Prime2), .Reset_E(Reset_E), .Reset_D(Reset_D), .E_button(E_button_out),
    .K_Button(K_button_out), .K(K), .Phi(Phi), .N(N), .E(E), .D(D), .REM1(Rem1), .REM2(Rem2));
  Button E_button (.out(E_button_out));
  Button K_button (.out(K_button_out));
  Keyboard keyboard_1 (.clk(button_1_out), .data(keyboard_1_data));  // open: re, clr, avail
  Button button_1 (.out(button_1_out));
  Button Button_2 (.out(Button_2_out));
  Button Button_3 (.out(Button_3_out));
  Encrypter encrypter_1 (
    .Letter(keyboard_1_data), .Load(Load), .Button(Button_2_out), .Encyrpted(Encrypted_Data), .Reset(Reset),
    .E_Count(Count));  // open: E, N
  Decrypter decrypter_1 (
    .Load(Load_2), .Button(Button_3_out), .D_Count(Count_2), .Reset(Reset_2), .Letter(decrypter_1_letter));  // open: Encrypted_Data, D, N
  Button Write (.out(Write_out));
  TTY tty_1 (.data(decrypter_1_letter), .clk(Write_out), .we(Clear), .clr(not_1_out));
  not not_1 (not_1_out, Clear);
endmodule

module KeyGenerator (
  input  [3:0] P,
  input  [3:0] Q,
  input  E_button,
  input  K_Button,
  input  Reset_E,
  input  Reset_D,
  output [7:0] N,
  output [7:0] E,
  output [7:0] D,
  output [7:0] REM1,
  output [7:0] REM2,
  output [15:0] K,
  output [7:0] Phi
);

  wire not_1_out, not_2_out;
  wire [7:0] bit_extender_1_out, bit_extender_2_out, subtractor_1_out, subtractor_2_out;
  wire [15:0] adder_1_out, bit_extender_3_out, bit_extender_4_out, divider_2_out, divider_2_rem,
       multiplier_3_out;

  assign bit_extender_1_out = {{4{1'b0}}, P};  // Bit_Extender bit_extender_1
  assign bit_extender_2_out = {{4{1'b0}}, Q};  // Bit_Extender bit_extender_2
  Multiplier multiplier_1 (.a(bit_extender_1_out), .b(bit_extender_2_out), .out(N));  // open: cin, cout
  Subtractor subtractor_1 (.a(bit_extender_1_out), .b(8'h1), .out(subtractor_1_out));  // open: bin, bout
  Subtractor subtractor_2 (.a(bit_extender_2_out), .b(8'h1), .out(subtractor_2_out));  // open: bin, bout
  Multiplier multiplier_2 (.a(subtractor_1_out), .b(subtractor_2_out), .out(Phi));  // open: cin, cout
  assign bit_extender_3_out = {{8{1'b0}}, Phi};  // Bit_Extender bit_extender_3
  Counter #(.width(16), .max('hffff)) counter_1 (
    .Q(K), .clk(K_Button), .clr(not_1_out));  // open: load, D, count, carry
  not not_1 (not_1_out, Reset_D);
  Counter #(.trigger("falling")) counter_2 (.Q(E), .clk(E_button), .clr(not_2_out));  // open: load, D, count, carry
  not not_2 (not_2_out, Reset_E);
  Multiplier #(.width(16)) multiplier_3 (.a(bit_extender_3_out), .b(K), .out(multiplier_3_out));  // open: cin, cout
  assign bit_extender_4_out = {{8{1'b0}}, E};  // Bit_Extender bit_extender_4
  Adder #(.width(16)) adder_1 (.a(multiplier_3_out), .b(16'h1), .out(adder_1_out));  // open: cin, cout
  Divider divider_1 (.a(Phi), .b(E), .rem(REM1));  // open: out, upper
  Divider #(.width(16)) divider_2 (
    .a(adder_1_out), .b(bit_extender_4_out), .out(divider_2_out), .rem(divider_2_rem));  // open: upper
  Bit_Extender #(.in_width(16), .out_width(8)) bit_extender_5 (.in(divider_2_out), .out(D));
  Bit_Extender #(.in_width(16), .out_width(8)) bit_extender_6 (.in(divider_2_rem), .out(REM2));
endmodule

module Encrypter (
  input  [6:0] Letter,
  input  [7:0] E,
  input  [7:0] N,
  input  Reset,
  input  Load,
  input  Button,
  output [7:0] Encyrpted,
  output [7:0] E_Count
);

  wire not_1_out, not_2_out;
  wire [6:0] subtractor_2_out;
  wire [7:0] subtractor_1_out;
  wire [25:0] bit_extender_1_out, bit_extender_2_out, divider_1_rem, multiplexer_1_out, multiplier_1_out,
       register_1_q;

  Subtractor subtractor_1 (.a(E), .b(8'h1), .out(subtractor_1_out));  // open: bin, bout
  Subtractor #(.width(7)) subtractor_2 (.a(Letter), .b(7'b1100001), .out(subtractor_2_out));  // open: bin, bout
  assign bit_extender_1_out = {{19{1'b0}}, subtractor_2_out};  // Bit_Extender bit_extender_1
  assign bit_extender_2_out = {{18{1'b0}}, N};  // Bit_Extender bit_extender_2
  Multiplier #(.width(26)) multiplier_1 (
    .a(bit_extender_1_out), .b(register_1_q), .out(multiplier_1_out));  // open: cin, cout
  Multiplexer #(.width(26)) multiplexer_1 (
    .in0(bit_extender_1_out), .in1(multiplier_1_out), .out(multiplexer_1_out), .sel(not_1_out));  // open: en
  not not_1 (not_1_out, Load);
  Register #(.width(26)) register_1 (
    .D(multiplexer_1_out), .Q(register_1_q), .clk(Button), .clr(not_2_out));  // open: en
  Counter counter_1 (
    .load(1'b1), .D(subtractor_1_out), .count(not_1_out), .Q(E_Count), .clk(Button), .clr(not_2_out));  // open: carry
  Divider #(.width(26)) divider_1 (.a(register_1_q), .b(bit_extender_2_out), .rem(divider_1_rem));  // open: out, upper
  not not_2 (not_2_out, Reset);
  Bit_Extender #(.in_width(26), .out_width(8)) bit_extender_3 (.in(divider_1_rem), .out(Encyrpted));
endmodule

module Decrypter (
  input  [7:0] Encrypted_Data,
  input  [7:0] D,
  input  [7:0] N,
  input  Load,
  input  Button,
  input  Reset,
  output [6:0] Letter,
  output [7:0] D_Count
);

  wire not_1_out, not_2_out;
  wire [6:0] bit_extender_3_out;
  wire [7:0] subtractor_1_out;
  wire [25:0] bit_extender_1_out, bit_extender_2_out, divider_1_rem, multiplexer_1_out, multiplier_1_out,
       register_1_q;

  Subtractor subtractor_1 (.a(D), .b(8'h1), .out(subtractor_1_out));  // open: bin, bout
  assign bit_extender_1_out = {{18{1'b0}}, Encrypted_Data};  // Bit_Extender bit_extender_1
  assign bit_extender_2_out = {{18{1'b0}}, N};  // Bit_Extender bit_extender_2
  Multiplier #(.width(26)) multiplier_1 (
    .a(bit_extender_1_out), .b(register_1_q), .out(multiplier_1_out));  // open: cin, cout
  Multiplexer #(.width(26)) multiplexer_1 (
    .in0(bit_extender_1_out), .in1(multiplier_1_out), .out(multiplexer_1_out), .sel(not_1_out));  // open: en
  not not_1 (not_1_out, Load);
  Register #(.width(26)) register_1 (
    .D(multiplexer_1_out), .Q(register_1_q), .clk(Button), .clr(not_2_out));  // open: en
  not not_2 (not_2_out, Reset);
  Counter counter_1 (
    .load(1'b1), .D(subtractor_1_out), .count(not_1_out), .Q(D_Count), .clk(Button), .clr(not_2_out));  // open: carry
  Divider #(.width(26)) divider_1 (.a(register_1_q), .b(bit_extender_2_out), .rem(divider_1_rem));  // open: out, upper
  Bit_Extender #(.in_width(26), .out_width(7)) bit_extender_3 (.in(divider_1_rem), .out(bit_extender_3_out));
  Adder #(.width(7)) adder_1 (.a(bit_extender_3_out), .b(7'b1100001), .out(Letter));  // open: cin, cout
endmodule
