// Logisim project key.circ as structural Verilog: 1 circuit, main circuit main
module main (
  input  [3:0] P,
  input  [3:0] Q,
  input  in_3,
  input  in_4,
  output [6:0] out_5,
  output [7:0] N,
  output [7:0] E,
  output [7:0] D,
  output [7:0] REM1,
  output [7:0] REM2,
  output [15:0] K,
  output [7:0] Phi
);

  wire button_1_out, button_2_out, button_3_out, not_1_out, not_2_out;
  wire [6:0] keyboard_1_data, keyboard_2_data, subtractor_3_out;
  wire [7:0] bit_extender_1_out, bit_extender_2_out, subtractor_1_out, subtractor_2_out;
  wire [15:0] adder_1_out, bit_extender_3_out, bit_extender_4_out, divider_2_out, divider_2_rem,
       multiplier_3_out;

  assign bit_extender_1_out = {{4{1'b0}}, P};  // Bit_Extender bit_extender_1
  assign bit_extender_2_out = {{4{1'b0}}, Q};  // Bit_Extender bit_extender_2
  Subtractor subtractor_1 (.a(bit_extender_1_out), .b(8'h1), .out(subtractor_1_out));  // open: bin, bout
  Subtractor subtractor_2 (.a(bit_extender_2_out), .b(8'h1), .out(subtractor_2_out));  // open: bin, bout
  Multiplier multiplier_1 (.a(bit_extender_1_out), .b(bit_extender_2_out), .out(N));  // open: cin, cout
  Multiplier multiplier_2 (.a(subtractor_1_out), .b(subtractor_2_out), .out(Phi));  // open: cin, cout
  assign bit_extender_3_out = {{8{1'b0}}, Phi};  // Bit_Extender bit_extender_3
  Counter #(.width(16), .max('hffff)) counter_1 (
    .Q(K), .clk(button_1_out), .clr(not_1_out));  // open: load, D, count, carry
  not not_1 (not_1_out, in_4);
  Button button_1 (.out(button_1_out));
  Counter #(.trigger("falling")) counter_2 (.Q(E), .clk(button_2_out), .clr(not_2_out));  // open: load, D, count, carry
  not not_2 (not_2_out, in_3);
  Button button_2 (.out(button_2_out));
  Multiplier #(.width(16)) multiplier_3 (.a(bit_extender_3_out), .b(K), .out(multiplier_3_out));  // open: cin, cout
  assign bit_extender_4_out = {{8{1'b0}}, E};  // Bit_Extender bit_extender_4
  Adder #(.width(16)) adder_1 (.a(multiplier_3_out), .b(16'h1), .out(adder_1_out));  // open: cin, cout
  Divider divider_1 (.a(Phi), .b(E), .rem(REM1));  // open: out, upper
  Divider #(.width(16)) divider_2 (
    .a(adder_1_out), .b(bit_extender_4_out), .out(divider_2_out), .rem(divider_2_rem));  // open: upper
  Bit_Extender #(.in_width(16), .out_width(8)) bit_extender_5 (.in(divider_2_out), .out(D));
  Bit_Extender #(.in_width(16), .out_width(8)) bit_extender_6 (.in(divider_2_rem), .out(REM2));
  Button button_3 (.out(button_3_out));
  Keyboard keyboard_1 (.clk(button_3_out), .data(keyboard_1_data));  // open: re, clr, avail
  Keyboard keyboard_2 (.data(keyboard_2_data));  // open: clk, re, clr, avail
  Subtractor #(.width(7)) subtractor_3 (
    .a(keyboard_1_data), .b(keyboard_2_data), .out(subtractor_3_out));  // open: bin, bout
  Bit_Extender #(.in_width(7), .out_width(8)) bit_extender_7 (.in(subtractor_3_out));  // open: out
endmodule
